# Fritzing sketch Watering (saved by Fritzing 0.9.2b)
breadboards: 1

parts:
  Watering = Arduino Uno (Rev3)
  VCC1 = Battery
  M1 = DC Motor
  Q1 = Basic FET P-Channel [package="TO220 [THT]"]
  D1 = Rectifier Diode [part_number=1N4001 package="300 mil [THT]"]
  T1 = LM35 Temperature Sensor [package="TO92 [THT]"]
  R1 = Photocell (LDR) [package=THT]
  R2 = Resistor [tolerance=±5% resistance=10k package=THT]

nets:
  N1: Watering.A0, T1.Vout
  N2: Watering.A1, R1.pin_1, R2.Pin_1
  N3: Watering.D11_PWM/MOSI, Q1.gate
  GND: Watering.GND, VCC1.-, Q1.source, T1.GND, R2.Pin_0
  N4: Watering.5V, T1.+Vs, R1.pin_0
  N5: VCC1.+, M1.pin_1, D1.cathode
  N6: M1.pin_2, Q1.drain, D1.anode
